// Logisim project lab3.circ as structural Verilog: 1 circuit, main circuit main
module main (
  input  I,
  input  Clock,
  input  Reset,
  output O
);

  wire and_1_out, and_2_out, and_3_out, and_4_out, not_1_out, or_1_out, X_q, X_qn, Y_q, Y_qn, Z_q, Z_qn;

  not not_1 (not_1_out, I);
  and and_1 (and_1_out, X_q, not_1_out);
  and and_2 (and_2_out, Y_q, Z_qn, not_1_out);
  or or_1 (or_1_out, and_1_out, and_2_out);
  and and_3 (and_3_out, Z_q, not_1_out);
  and and_4 (and_4_out, X_qn, Y_qn, not_1_out);
  D_Flip_Flop X (.D(or_1_out), .clk(Clock), .Q(X_q), .Qn(X_qn), .reset(Reset));  // open: preset
  D_Flip_Flop Y (.D(and_3_out), .clk(Clock), .Q(Y_q), .Qn(Y_qn), .reset(Reset));  // open: preset
  D_Flip_Flop Z (.D(and_4_out), .clk(Clock), .Q(Z_q), .Qn(Z_qn), .reset(Reset));  // open: preset
  and and_5 (O, X_q, not_1_out);
endmodule
