// Logisim project modules.circ as structural Verilog: 5 circuits, main circuit top_stopwatch
module top_stopwatch (
  input  reset_n_pin,
  input  sys_clk_pin,
  input  key_a_pin,
  input  key_b_pin,
  input  key_c_pin,
  output seg_pins_6_0,
  output an_pins_3_0,
  output led_minute_pin,
  output led_alarm_pin
);

  wire button_interface_debounce_a_key_pulse_out, button_interface_debounce_b_key_pulse_out,
       button_interface_debounce_c_key_pulse_out, clk_divider_counter_1_blink_clk_enable,
       clk_divider_counter_1_max_time_reached, clk_divider_counter_1_min_out,
       clk_divider_counter_1_ms_bcd_ones_out_3_0_b4a6c656,
       clk_divider_counter_1_ms_bcd_tens_out_3_0_450e3299, clk_divider_counter_1_scan_clk_enable,
       clk_divider_counter_1_sec_bcd_ones_out_3_0_70daa37a,
       clk_divider_counter_1_sec_bcd_tens_out_3_0_3d4b871d, not_1_out, state_controller_1_alarm_active_out,
       state_controller_1_timer_reset_cmd_out, state_controller_1_timer_run_en_out;

  not not_1 (not_1_out, reset_n_pin);
  button_interface_debounce button_interface_debounce_a (
    .clk(sys_clk_pin), .reset_n(not_1_out), .key_raw_in(key_a_pin),
    .key_pulse_out(button_interface_debounce_a_key_pulse_out));
  button_interface_debounce button_interface_debounce_b (
    .clk(sys_clk_pin), .reset_n(not_1_out), .key_raw_in(key_b_pin),
    .key_pulse_out(button_interface_debounce_b_key_pulse_out));
  button_interface_debounce button_interface_debounce_c (
    .clk(sys_clk_pin), .key_raw_in(key_c_pin), .key_pulse_out(button_interface_debounce_c_key_pulse_out));  // open: reset_n
  state_controller state_controller_1 (
    .clk(sys_clk_pin), .reset_n(not_1_out), .key_a_pulse(button_interface_debounce_a_key_pulse_out),
    .key_b_pulse(button_interface_debounce_b_key_pulse_out),
    .key_c_pulse(button_interface_debounce_c_key_pulse_out),
    .max_time_reached_in(clk_divider_counter_1_max_time_reached),
    .timer_run_en_out(state_controller_1_timer_run_en_out),
    .timer_reset_cmd_out(state_controller_1_timer_reset_cmd_out),
    .alarm_active_out(state_controller_1_alarm_active_out));
  clk_divider_counter clk_divider_counter_1 (
    .clk(sys_clk_pin), .reset_n(not_1_out), .timer_run_en(state_controller_1_timer_run_en_out),
    .timer_reset_cmd(state_controller_1_timer_reset_cmd_out),
    .ms_bcd_tens_out_3_0_450e3299(clk_divider_counter_1_ms_bcd_tens_out_3_0_450e3299),
    .ms_bcd_ones_out_3_0_b4a6c656(clk_divider_counter_1_ms_bcd_ones_out_3_0_b4a6c656),
    .sec_bcd_tens_out_3_0_3d4b871d(clk_divider_counter_1_sec_bcd_tens_out_3_0_3d4b871d),
    .sec_bcd_ones_out_3_0_70daa37a(clk_divider_counter_1_sec_bcd_ones_out_3_0_70daa37a),
    .min_out(clk_divider_counter_1_min_out), .max_time_reached(clk_divider_counter_1_max_time_reached),
    .scan_clk_enable(clk_divider_counter_1_scan_clk_enable),
    .blink_clk_enable(clk_divider_counter_1_blink_clk_enable));
  display_driver display_driver_1 (
    .clk(sys_clk_pin), .reset_n(not_1_out),
    .ms_bcd_tens_in(clk_divider_counter_1_ms_bcd_tens_out_3_0_450e3299),
    .ms_bcd_ones_in(clk_divider_counter_1_ms_bcd_ones_out_3_0_b4a6c656),
    .sec_bcd_tens_in(clk_divider_counter_1_sec_bcd_tens_out_3_0_3d4b871d),
    .sec_bcd_ones_in(clk_divider_counter_1_sec_bcd_ones_out_3_0_70daa37a),
    .min_in(clk_divider_counter_1_min_out), .alarm_active_in(state_controller_1_alarm_active_out),
    .scan_clk_enable_in(clk_divider_counter_1_scan_clk_enable),
    .blink_clk_enable_in(clk_divider_counter_1_blink_clk_enable), .seg_out_6_0_f79ae683(seg_pins_6_0),
    .an_out_3_0_17c24b36(an_pins_3_0), .led_minute_out(led_minute_pin), .led_alarm_out(led_alarm_pin));
endmodule

module button_interface_debounce (
  input  clk,
  input  reset_n,
  input  key_raw_in,
  output key_pulse_out
);
endmodule

module clk_divider_counter (
  input  clk,
  input  reset_n,
  input  timer_run_en,
  input  timer_reset_cmd,
  output ms_bcd_tens_out_3_0_450e3299,
  output ms_bcd_ones_out_3_0_b4a6c656,
  output sec_bcd_tens_out_3_0_3d4b871d,
  output sec_bcd_ones_out_3_0_70daa37a,
  output min_out,
  output max_time_reached,
  output scan_clk_enable,
  output blink_clk_enable
);
endmodule

module display_driver (
  input  clk,
  input  reset_n,
  input  ms_bcd_tens_in,
  input  ms_bcd_ones_in,
  input  sec_bcd_tens_in,
  input  sec_bcd_ones_in,
  input  min_in,
  input  alarm_active_in,
  input  scan_clk_enable_in,
  input  blink_clk_enable_in,
  output seg_out_6_0_f79ae683,
  output an_out_3_0_17c24b36,
  output led_minute_out,
  output led_alarm_out
);
endmodule

module state_controller (
  input  clk,
  input  reset_n,
  input  key_a_pulse,
  input  key_b_pulse,
  input  key_c_pulse,
  input  max_time_reached_in,
  output timer_run_en_out,
  output timer_reset_cmd_out,
  output alarm_active_out
);
endmodule
