// Logisim project lab2.circ as structural Verilog: 3 circuits, main circuit main
module main (
  input  A_3,
  input  A_2,
  input  A_1,
  input  A_0,
  output B_2,
  output B_1,
  output B_0
);

  wire nand_1_out, nand_2_out, nand_3_out, nand_4_out, nand_5_out, nand_6_out, nand_7_out, nand_8_out,
       nand_9_out, nand_10_out, nand_11_out, not_1_out, not_2_out, not_3_out, not_4_out;

  not not_1 (not_1_out, A_3);
  not not_2 (not_2_out, A_2);
  not not_3 (not_3_out, A_1);
  not not_4 (not_4_out, A_0);
  nand nand_1 (nand_1_out, A_3, A_2, A_0);
  nand nand_2 (nand_2_out, A_3, A_2, A_1);
  nand nand_3 (nand_3_out, not_1_out, A_2);
  nand nand_4 (nand_4_out, A_3, not_2_out);
  nand nand_5 (nand_5_out, not_1_out, A_1, A_0);
  nand nand_6 (nand_6_out, A_3, not_3_out, not_4_out);
  nand nand_7 (nand_7_out, not_2_out, not_3_out, A_0);
  nand nand_8 (nand_8_out, not_2_out, A_1, not_4_out);
  nand nand_9 (nand_9_out, not_1_out, A_2, A_1, A_0);
  nand nand_10 (nand_10_out, A_3, not_2_out);
  nand nand_11 (nand_11_out, A_3, not_3_out, not_4_out);
  nand nand_12 (B_2, nand_1_out, nand_2_out);
  nand nand_13 (B_1, nand_3_out, nand_4_out, nand_5_out, nand_6_out);
  nand nand_14 (B_0, nand_7_out, nand_8_out, nand_9_out, nand_10_out, nand_11_out);
endmodule

module origin (
  input  A_3,
  input  A_2,
  input  A_1,
  input  A_0,
  output B_2,
  output B_1,
  output B_0
);

  wire and_1_out, and_2_out, and_3_out, and_4_out, and_5_out, and_6_out, and_7_out, and_8_out, and_9_out,
       and_10_out, and_11_out, not_1_out, not_2_out, not_3_out, not_4_out;

  not not_1 (not_1_out, A_3);
  not not_2 (not_2_out, A_2);
  not not_3 (not_3_out, A_1);
  not not_4 (not_4_out, A_0);
  and and_1 (and_1_out, A_3, A_2, A_0);
  and and_2 (and_2_out, A_3, A_2, A_1);
  and and_3 (and_3_out, not_1_out, A_2);
  and and_4 (and_4_out, A_3, not_2_out);
  and and_5 (and_5_out, not_1_out, A_1, A_0);
  and and_6 (and_6_out, A_3, not_3_out, not_4_out);
  and and_7 (and_7_out, not_2_out, not_3_out, A_0);
  and and_8 (and_8_out, not_2_out, A_1, not_4_out);
  and and_9 (and_9_out, not_1_out, A_2, A_1, A_0);
  and and_10 (and_10_out, A_3, not_2_out);
  and and_11 (and_11_out, A_3, not_3_out, not_4_out);
  or or_1 (B_2, and_1_out, and_2_out);
  or or_2 (B_1, and_3_out, and_4_out, and_5_out, and_6_out);
  or or_3 (B_0, and_7_out, and_8_out, and_9_out, and_10_out, and_11_out);
endmodule

module origin_twoinputgateonly (
  input  A_3,
  input  A_2,
  input  A_1,
  input  A_0,
  output B_2,
  output B_1,
  output B_0
);

  wire and_1_out, and_2_out, and_3_out, and_4_out, and_5_out, and_6_out, and_7_out, and_8_out, and_9_out,
       and_10_out, and_11_out, and_12_out, and_13_out, and_14_out, and_15_out, and_16_out, and_17_out,
       and_18_out, and_19_out, and_20_out, not_1_out, not_2_out, not_3_out, not_4_out, or_2_out, or_3_out,
       or_4_out, or_6_out, or_7_out;

  not not_1 (not_1_out, A_3);
  not not_2 (not_2_out, A_2);
  not not_3 (not_3_out, A_1);
  not not_4 (not_4_out, A_0);
  and and_1 (and_1_out, A_3, A_2);
  and and_2 (and_2_out, A_3, A_2);
  and and_3 (and_3_out, not_1_out, A_1);
  and and_4 (and_4_out, A_3, not_3_out);
  and and_5 (and_5_out, not_2_out, not_3_out);
  and and_6 (and_6_out, not_2_out, A_1);
  and and_7 (and_7_out, and_1_out, A_0);
  and and_8 (and_8_out, and_2_out, A_1);
  and and_9 (and_9_out, not_1_out, A_2);
  and and_10 (and_10_out, A_3, not_2_out);
  and and_11 (and_11_out, and_3_out, A_0);
  and and_12 (and_12_out, and_4_out, not_4_out);
  and and_13 (and_13_out, and_5_out, A_0);
  and and_14 (and_14_out, and_6_out, not_4_out);
  and and_15 (and_15_out, not_1_out, A_2);
  and and_16 (and_16_out, A_1, A_0);
  and and_17 (and_17_out, A_3, not_3_out);
  or or_1 (B_2, and_7_out, and_8_out);
  or or_2 (or_2_out, and_9_out, and_10_out);
  or or_3 (or_3_out, and_11_out, and_12_out);
  or or_4 (or_4_out, and_13_out, and_14_out);
  and and_18 (and_18_out, and_15_out, and_16_out);
  and and_19 (and_19_out, A_3, not_2_out);
  and and_20 (and_20_out, and_17_out, not_4_out);
  or or_5 (B_1, or_2_out, or_3_out);
  or or_6 (or_6_out, or_4_out, and_18_out);
  or or_7 (or_7_out, and_19_out, and_20_out);
  or or_8 (B_0, or_6_out, or_7_out);
endmodule
